// Digital circuit CPU_main.dig as structural Verilog
module CPU_main (
  input  clk
);

  wire Acc_in, Acc_out, ALU_out, B_reg_in, CLR_T, IR_in, IR_out, MAR_in, MEM_out, PC_enable, PC_load, PC_out,
       RESET, START;
  wire [2:0] ALU_Op, COUNTER;
  wire [3:0] IR_q, OPCODE;
  wire [7:0] Acc_q, alu_main_1_s_out, and_1_out, B_reg_q, MAR_q, PC_out_2, W_BUS;

  Button u_RESET (.out(RESET));
  // Probe on RESET
  // Probe on clk
  CounterPreset #(.Bits(8)) PC (
    .en(PC_enable), .C(clk), .dir(1'b0), .in(W_BUS), .ld(PC_load), .clr(RESET), .out(PC_out_2));  // open: ovf
  // Probe on COUNTER
  // Probe on OPCODE
  // Probe on {OPCODE, COUNTER}
  // Probe on {OPCODE, COUNTER}
  ROM #(.AddrBits(7), .Bits(16)) CONTROL_ROM (
    .A({OPCODE, COUNTER}), .sel(1'b1),
    .D({ALU_Op, PC_out, MAR_in, MEM_out, IR_in, IR_out, Acc_in, Acc_out, ALU_out, B_reg_in, PC_enable, PC_load, CLR_T, START}));
  assign W_BUS = PC_out ? PC_out_2 : 8'bz;  // Driver driver_1
  // Probe PC_PROBE on PC_out_2
  Counter #(.Bits(3)) u_Counter (.en(1'b1), .C(clk), .clr(CLR_T), .out(COUNTER));  // open: ovf
  // Probe on {ALU_Op, PC_out, MAR_in, MEM_out, IR_in, IR_out, Acc_in, Acc_out, ALU_out, B_reg_in, PC_enable, PC_load, CLR_T, START}
  // Probe on COUNTER
  Register #(.Bits(8)) IR (.D(W_BUS), .C(clk), .en(IR_in), .Q({OPCODE, IR_q}));
  assign and_1_out = {OPCODE, IR_q} & 8'hf;  // And and_1, 8 bits wide
  // Probe on {OPCODE, IR_q}
  // Probe on OPCODE
  // Probe on OPCODE
  // Probe on and_1_out
  // Probe on ALU_out
  // Probe on IR_out
  // Probe on MEM_out
  // Probe on PC_out
  Register #(.Bits(8)) B_reg (.D(W_BUS), .C(clk), .en(B_reg_in), .Q(B_reg_q));
  Register #(.Bits(8)) Acc (.D(W_BUS), .C(clk), .en(Acc_in), .Q(Acc_q));
  assign W_BUS = IR_out ? and_1_out : 8'bz;  // Driver driver_2
  // Probe on B_reg_q
  // Probe on W_BUS
  Register #(.Bits(8)) MAR (.D(W_BUS), .C(clk), .en(MAR_in), .Q(MAR_q));
  ALU_main alu_main_1 (
    .A_in(Acc_q), .B_in(B_reg_q), .ALU_op(ALU_Op), .CLK(clk), .START(START), .S_out(alu_main_1_s_out));  // open: Z_flag, ALU_busy
  assign W_BUS = Acc_out ? Acc_q : 8'bz;  // Driver driver_3
  // Probe ACC_PROBE on Acc_q
  // Probe MAR_PROBE on MAR_q
  // Probe on MAR_q
  assign W_BUS = ALU_out ? alu_main_1_s_out : 8'bz;  // Driver driver_4
  EEPROMDualPort #(.AddrBits(8), .Bits(8)) eepromdualport_1 (
    .A(MAR_q), .Din(W_BUS), .str(START), .C(clk), .ld(MEM_out), .D(W_BUS));
  // Probe on W_BUS

  // Notes on the sheet:
  //   contents of CONTROL_ROM (hex, n*v repeats v):
  //   1800,8,600,900,480,2,0,0,1800,8,600,900,410,a0,2,0,1800,8,600
  //   ,900,41,2,0,0,1800,8,600,904,2
  //   contents of eepromdualport_1 (hex, n*v repeats v):
  //   a,35,1b,0,0,2c,4*0,77,11,77
endmodule
