// Digital circuit multiplier_4bit.dig as structural Verilog
module multiplier_4bit (
  input  [3:0] A,
  input  [3:0] B,
  input  CLK,
  input  START,
  output [7:0] P
);

  wire and_1_out, counter_4bit_1_zero, rs_ff_as_1_nq, rs_ff_as_1_q;
  wire [7:0] adder_8bit_1_s, bitextender_1_out;

  and and_1 (and_1_out, CLK, rs_ff_as_1_q);
  D_FF_AS #(.Bits(8)) P_reg (.Set(1'b0), .D(adder_8bit_1_s), .C(and_1_out), .Clr(START), .Q(P));  // open: nQ
  BitExtender #(.inputBits(4), .outputBits(8)) bitextender_1 (.in(A), .out(bitextender_1_out));
  counter_4bit counter_4bit_1 (
    .D(B), .CLK(CLK), .LOAD(START), .EN(rs_ff_as_1_q), .ZERO(counter_4bit_1_zero));  // open: Q
  adder_8bit adder_8bit_1 (.A(P), .B(bitextender_1_out), .Cin(1'b0), .S(adder_8bit_1_s));  // open: Cout
  RS_FF_AS rs_ff_as_1 (.S(START), .R(counter_4bit_1_zero), .Q(rs_ff_as_1_q), .nQ(rs_ff_as_1_nq));
  LED DONE (.in(rs_ff_as_1_nq));
endmodule
